// Logisim project 16-bit ALU.circ as structural Verilog
module _1_bit_ALU (
  input  A,
  input  B,
  input  [1:0] Operation,
  input  Cin,
  input  Sub,
  output Result,
  output Cout
);

  wire adder_1_out, AND_out, OR_out, xor_1_out, XOR_2_out;

  xor xor_1 (xor_1_out, B, Sub);
  and AND (AND_out, A, B);
  or OR (OR_out, A, B);
  xor XOR_2 (XOR_2_out, A, B);
  Adder #(.width(1)) adder_1 (.a(A), .b(xor_1_out), .out(adder_1_out), .cin(Cin), .cout(Cout));
  Multiplexer #(.select(2)) multiplexer_1 (
    .in0(AND_out), .in1(OR_out), .in2(XOR_2_out), .in3(adder_1_out), .out(Result), .sel(Operation));  // open: en
endmodule

module _16_bits_ALU (
  input  Cin,
  input  [15:0] A,
  input  [15:0] B,
  output Cout
);

  wire n1_bit_alu_1_cout, n1_bit_alu_2_cout, n1_bit_alu_3_cout, n1_bit_alu_4_cout, n1_bit_alu_5_cout,
       n1_bit_alu_6_cout, n1_bit_alu_7_cout, n1_bit_alu_8_cout, n1_bit_alu_9_cout, n1_bit_alu_10_cout,
       n1_bit_alu_11_cout, n1_bit_alu_12_cout, n1_bit_alu_13_cout, n1_bit_alu_14_cout, n1_bit_alu_15_cout;

  _1_bit_ALU u_1_bit_alu_1 (.A(A[0]), .B(B[0]), .Cin(Cin), .Cout(n1_bit_alu_1_cout));  // open: Result, Sub, Operation
  _1_bit_ALU u_1_bit_alu_2 (
    .A(A[1]), .B(B[1]), .Cin(n1_bit_alu_1_cout), .Cout(n1_bit_alu_2_cout));  // open: Result, Sub, Operation
  _1_bit_ALU u_1_bit_alu_3 (
    .A(A[2]), .B(B[2]), .Cin(n1_bit_alu_2_cout), .Cout(n1_bit_alu_3_cout));  // open: Result, Sub, Operation
  _1_bit_ALU u_1_bit_alu_4 (
    .A(A[3]), .B(B[3]), .Cin(n1_bit_alu_3_cout), .Cout(n1_bit_alu_4_cout));  // open: Result, Sub, Operation
  _1_bit_ALU u_1_bit_alu_5 (
    .A(A[4]), .B(B[4]), .Cin(n1_bit_alu_4_cout), .Cout(n1_bit_alu_5_cout));  // open: Result, Sub, Operation
  _1_bit_ALU u_1_bit_alu_6 (
    .A(A[5]), .B(B[5]), .Cin(n1_bit_alu_5_cout), .Cout(n1_bit_alu_6_cout));  // open: Result, Sub, Operation
  _1_bit_ALU u_1_bit_alu_7 (
    .A(A[6]), .B(B[6]), .Cin(n1_bit_alu_6_cout), .Cout(n1_bit_alu_7_cout));  // open: Result, Sub, Operation
  _1_bit_ALU u_1_bit_alu_8 (
    .A(A[7]), .B(B[7]), .Cin(n1_bit_alu_7_cout), .Cout(n1_bit_alu_8_cout));  // open: Result, Sub, Operation
  _1_bit_ALU u_1_bit_alu_9 (
    .A(A[8]), .B(B[8]), .Cin(n1_bit_alu_8_cout), .Cout(n1_bit_alu_9_cout));  // open: Result, Sub, Operation
  _1_bit_ALU u_1_bit_alu_10 (
    .A(A[9]), .B(B[9]), .Cin(n1_bit_alu_9_cout), .Cout(n1_bit_alu_10_cout));  // open: Result, Sub, Operation
  _1_bit_ALU u_1_bit_alu_11 (
    .A(A[10]), .B(B[10]), .Cin(n1_bit_alu_10_cout), .Cout(n1_bit_alu_11_cout));  // open: Result, Sub, Operation
  _1_bit_ALU u_1_bit_alu_12 (
    .A(A[11]), .B(B[11]), .Cin(n1_bit_alu_11_cout), .Cout(n1_bit_alu_12_cout));  // open: Result, Sub, Operation
  _1_bit_ALU u_1_bit_alu_13 (
    .A(A[12]), .B(B[12]), .Cin(n1_bit_alu_12_cout), .Cout(n1_bit_alu_13_cout));  // open: Result, Sub, Operation
  _1_bit_ALU u_1_bit_alu_14 (
    .A(A[13]), .B(B[13]), .Cin(n1_bit_alu_13_cout), .Cout(n1_bit_alu_14_cout));  // open: Result, Sub, Operation
  _1_bit_ALU u_1_bit_alu_15 (
    .A(A[14]), .B(B[14]), .Cin(n1_bit_alu_14_cout), .Cout(n1_bit_alu_15_cout));  // open: Result, Sub, Operation
  _1_bit_ALU u_1_bit_alu_16 (
    .A(A[15]), .B(B[15]), .Cin(n1_bit_alu_15_cout), .Cout(Cout));  // open: Result, Sub, Operation
endmodule
